# Fritzing sketch phonebooth_mainboard (saved by Fritzing 0.6.3b)
perfboards: 1

parts:
  J2 = female pin header, 2 pins [form="♀ (female)"]
  J3 = female pin header, 2 pins [form="♀ (female)"]
  J4 = female pin header, 2 pins [form="♀ (female)"]
  J5 = female pin header, 2 pins [form="♀ (female)"]
  J6 = female pin header, 2 pins [form="♀ (female)"]
  J7 = female pin header, 2 pins [form="♀ (female)"]
  J8 = female pin header, 2 pins [form="♀ (female)"]
  J9 = female pin header, 2 pins [form="♀ (female)"]
  J10 = female pin header, 2 pins [form="♀ (female)"]
  J11 = female pin header, 2 pins [form="♀ (female)"]
  J12 = female pin header, 2 pins [form="♀ (female)"]
  J13 = female pin header, 2 pins [form="♀ (female)"]
  J1 = female pin header, 12 pins [form="♀ (female)"]
  Arduino1 = Arduino Mega
  J18 = female pin header, 10 pins [form="♀ (female)"]
  J19 = female pin header, 2 pins [form="♀ (female)"]
  J20 = female pin header, 2 pins [form="♀ (female)"]
  J21 = female pin header, 2 pins [form="♀ (female)"]
  J22 = female pin header, 2 pins [form="♀ (female)"]
  J23 = female pin header, 2 pins [form="♀ (female)"]
  J24 = female pin header, 2 pins [form="♀ (female)"]
  J25 = female pin header, 2 pins [form="♀ (female)"]
  J26 = female pin header, 2 pins [form="♀ (female)"]
  J27 = female pin header, 2 pins [form="♀ (female)"]
  J28 = female pin header, 2 pins [form="♀ (female)"]
  J29 = female pin header, 2 pins [form="♀ (female)"]
  J30 = female pin header, 2 pins [form="♀ (female)"]
  LED1 = LED - 5mm [color="Red (633nm)" package="5 mm [THT]"]
  R1 = Resistor [tolerance=±5% resistance=220 package=THT]
  LED2 = LED - 5mm [color="Red (633nm)" package="5 mm [THT]"]
  R2 = Resistor [tolerance=±5% resistance=220 package=THT]
  LED3 = LED - 5mm [color="Red (633nm)" package="5 mm [THT]"]
  R3 = Resistor [tolerance=±5% resistance=220 package=THT]
  LED4 = LED - 5mm [color="Red (633nm)" package="5 mm [THT]"]
  R4 = Resistor [tolerance=±5% resistance=220 package=THT]
  LED5 = LED - 5mm [color="Red (633nm)" package="5 mm [THT]"]
  R5 = Resistor [tolerance=±5% resistance=220 package=THT]
  S1 = Pushbutton [package="[THT]"]
  J31 = female pin header, 8 pins [form="♀ (female)"]
  J32 = female pin header, 8 pins [form="♀ (female)"]

nets (from the pcb view):
  N1: J2.pin1, Arduino1.A11
  N2: J2.pin2, J3.pin2, J4.pin2, J5.pin2, J6.pin2, J7.pin2, J8.pin2, J9.pin2, J10.pin2, J11.pin2, J12.pin2, J13.pin2, Arduino1.GND, J18.pin4, J19.pin2, J20.pin2, J21.pin2, J22.pin2, J23.pin2, J24.pin2, J25.pin2, J26.pin2, J27.pin2, J28.pin2, J29.pin2, J30.pin2, LED1.cathode, LED2.cathode, LED3.cathode, LED4.cathode, LED5.cathode, S1.Pin_4
  N3: J3.pin1, Arduino1.A10
  N4: J4.pin1, Arduino1.A9
  N5: J5.pin1, Arduino1.A8
  N6: J6.pin1, Arduino1.A7
  N7: J7.pin1, Arduino1.A6
  N8: J8.pin1, Arduino1.A5
  N9: J9.pin1, Arduino1.A1
  N10: J10.pin1, Arduino1.A4
  N11: J11.pin1, Arduino1.A3
  N12: J12.pin1, Arduino1.A2
  N13: J13.pin1, Arduino1.A0
  N14: J1.pin1, J1.pin2, J1.pin3, J1.pin4, J1.pin5, J1.pin6, J1.pin7, J1.pin8, J1.pin9, J1.pin10, J1.pin11, J1.pin12, Arduino1.+5V#18, J18.pin6
  N15: Arduino1.D13, J30.pin1
  N16: Arduino1.D12, J28.pin1
  N17: Arduino1.D11, J29.pin1
  N18: Arduino1.D10, J27.pin1
  N19: Arduino1.D9, J19.pin1
  N20: Arduino1.D8, J20.pin1
  N21: Arduino1.D7, J21.pin1, R1.Pin_1
  N22: Arduino1.D6, J22.pin1, R2.Pin_1
  N23: Arduino1.D5, J26.pin1, R3.Pin_1
  N24: Arduino1.D4, J24.pin1, R4.Pin_1
  N25: Arduino1.D3, J25.pin1, R5.Pin_1
  N26: Arduino1.D2, J23.pin1
  N27: Arduino1.D1TX, J18.pin7
  N28: Arduino1.D0RX, J18.pin8
  N29: Arduino1.RST, S1.Pin_1
  N30: LED1.anode, R1.Pin_0
  N31: LED2.anode, R2.Pin_0
  N32: LED3.anode, R3.Pin_0
  N33: LED4.anode, R4.Pin_0
  N34: LED5.anode, R5.Pin_0
  N35: J31.pin1, J32.pin1
  N36: J31.pin2, J32.pin2
  N37: J31.pin3, J32.pin3
  N38: J31.pin4, J32.pin4
  N39: J31.pin5, J32.pin5
  N40: J31.pin6, J32.pin6
  N41: J31.pin7, J32.pin7
  N42: J31.pin8, J32.pin8

notes:
  5v x12 to patchboard sets
  xbee adafruit adapter socket
  pwn for adapter led's (up to 12)
  adapters to analog pins
  button, knob (rotary encoder), label LED's
  sd card reader?, LCD display?, debug/setup toggle switch
  CIA
  WFB
  PBE
  MB
  v 1.0
